# Fritzing sketch car_buddy_fritzing (saved by Fritzing 0.9.5d)
breadboards: 2

parts:
  esp1 = ESP32 DevKitc V4
  DS1 = DS18B20 1-Wire Temperature Sensor [part_number=DS18B20]
  LCD1 = 2.8" SPI TFT Module [part_number=MSP2807]
  SP1 = SPEAKER [package=pcb_mount_speaker]
  R1 = Resistor [tolerance=±5% resistance=220 package="1206 [SMD]"]
  パーツ1 = InvenSense MPU6050
  M1 = PAM8403 Stereo Amplifier [part_number=HW-104]

nets:
  N1: esp1.IO15, LCD1.pin3
  N2: esp1.IO2, LCD1.pin5
  N3: esp1.IO4, LCD1.pin4
  N4: esp1.IO5, LCD1.pin18
  N5: esp1.IO18, LCD1.pin7, LCD1.pin15
  N6: esp1.IO19, LCD1.pin9, LCD1.pin16
  N7: esp1.IO21, パーツ1.SDA
  N8: esp1.IO22, パーツ1.SCL
  N9: esp1.IO23, LCD1.pin6, LCD1.pin17
  3V3: esp1.3V3, DS1.VDD, LCD1.pin1, LCD1.pin8, R1.Pin_0, パーツ1.VCC
  N10: esp1.IO25, M1.INPUTL
  N11: esp1.IO26, M1.INPUTR
  N12: esp1.IO14, DS1.DQ, R1.Pin_1
  GND: esp1.GND#32, DS1.GND, LCD1.pin2, パーツ1.GND, パーツ1.AD0, M1.POWER-, M1.INPUTG
  N13: esp1.5V, M1.POWER+
  N14: SP1.+, M1.LOUT-
  N15: SP1.-, M1.LOUT+

custom parts:
  ESP32 DevKitc V4: ESP32-DevKitC board with ESP32-WROOM-32 module. ESP32-DevKitC V4 is a small-sized ESP32-based development board produced by Espressif. Most of the pins on the ESP module are broken out to the pin headers on the board. The pins D0, D1, D2, D3, CMD and CLK are used internally for communication between ESP32 and SPI flash memory. They are grouped on both sides near the USB connector. Avoid using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
  2.8" SPI TFT Module: A generic 2.8 inch LCD TFT 320x240 display with touchscreen and SD card slot. Uses the ILI9341 controller, like the Adafruit displays of this size uses.
  PAM8403 Stereo Amplifier: PAM8403 stereo amplifier module Descriptive words Links: PAM8403 product datasheet
